# Fritzing sketch pi-datamon (saved by Fritzing 1.0.8)
breadboards: 1

parts:
  Raspberry_Pi_3B+ = Raspberry Pi 3 [part_number=RPI-3-V1.2]
  Tactile_Push_Button = Pushbutton [package="[THT]"]
  HC-SR04_Ultrasonic_Sensor = HC-SR04 Ultrasonic Distance Sensor
  SSD1306_0_96"_4P_I2C_Monochrome_OLED_Display = OLED 128x64 I2C Monochrome Display GND-VDD
  AHT20/1_Temperature/Humidity_I2C_Sensor = AHT2x module
  R1 = Resistor [tolerance=±5% power=0.25W resistance=2.2k package=THT]
  R2 = Resistor [tolerance=±5% power=0.25W resistance=2.2k package=THT]

nets:
  3V3: Raspberry_Pi_3B+.3v3, Raspberry_Pi_3B+.3V3, SSD1306_0_96"_4P_I2C_Monochrome_OLED_Display.VDD, AHT20/1_Temperature/Humidity_I2C_Sensor.Pin_4
  N1: Raspberry_Pi_3B+.GPIO2, SSD1306_0_96"_4P_I2C_Monochrome_OLED_Display.SDA, AHT20/1_Temperature/Humidity_I2C_Sensor.Pin_1
  N2: Raspberry_Pi_3B+.GPIO3, SSD1306_0_96"_4P_I2C_Monochrome_OLED_Display.SCK, AHT20/1_Temperature/Humidity_I2C_Sensor.Pin_2
  N3: Raspberry_Pi_3B+.GPIO4, HC-SR04_Ultrasonic_Sensor.TRIG
  GND: Raspberry_Pi_3B+.GND, Tactile_Push_Button.Pin_3, Tactile_Push_Button.Pin_4, HC-SR04_Ultrasonic_Sensor.GND, SSD1306_0_96"_4P_I2C_Monochrome_OLED_Display.GND, AHT20/1_Temperature/Humidity_I2C_Sensor.Pin_3, R2.Pin_1
  N4: Raspberry_Pi_3B+.GPIO27, R1.Pin_0, R2.Pin_0
  N5: Raspberry_Pi_3B+.GPIO26, Tactile_Push_Button.Pin_1, Tactile_Push_Button.Pin_2
  5V: Raspberry_Pi_3B+.5V, HC-SR04_Ultrasonic_Sensor.VCC
  N6: HC-SR04_Ultrasonic_Sensor.ECHO, R1.Pin_1

notes:
  PI DATAMON CONNECTIONS
  AHT20/1 I2C Temperature/Humidity Sensor
  VIN --> 3.3v Rail (Pin 1)
  GND --> GND Rail (Pin 6)
  SCL --> GPIO3 Serial Clock (I2C) (Pin 5)
  SDA --> GPIO2 Serial Data (I2X) (Pin 3)
  SSD1306 0.96" 4P I2C Monochrome OLED Display
  GND --> GND Rail (Pin 6)
  VDD --> 3.3v Rail (Pin 1)
  SCL --> GPIO3 Serial Clock (I2C) (Pin 5)
  SDA --> GPIO2 Serial Data (I2X) (Pin 3)
  HC-SR04 Ultrasonic Sensor
  Vcc --> 5v (Pin 2)
  Trig --> GPIO4 (Pin 7)
  Echo --> GPIO27 (Pin 13)
  Gnd --> GND Rail (Pin 6)
  The AHT20/1 sensor can be flipped horizontally to show the neater icons. If flipped, reverse the left-to-right wiring.
  The HC-SR04 sensor is connected with wires to show the other wires more clearly. It should be directly connected to the breadboard like the other sensors.
  The voltage divider in the diagram for Echo output uses two 2.2k resistors, but the real project uses 2k resistors.
  Vin=5V
  R1=2k ohms
  R2=2k ohms
  Vout=(Vin*R1)/(R1+R2)
  Vout=(5*2)/(2+2)
  Vout=10/4
  Vout=2.5V
  SDA
  SCL
  Trig
  Echo
  Active-LOW Button
  pull_up=True
  --> GPIO26 (Pin 37)

custom parts:
  OLED 128x64 I2C Monochrome Display GND-VDD: OLED 128x64 I2C Monochrome Display. Note: there are two variants of this part, this one is the GND VDD SCK SDA variant. The other is VDD GND SCK SDA. Make sure you select the part that matches your module as using the incorrect part will probably destroy your module! In addition the mounting holes are marked on silkscreen but not by default drilled. If you want drilled mounting holes, copy a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
  AHT2x module: AHT10 AHT20 AHT21 High Precision Digital Temperature and Humidity Sensor Measurement Module I2C Communication.
